// Logisim project t6_wash_e2e.circ as structural Verilog: 23 circuits, main circuit tb_main
module tb_main (
  output [15:0] IFID_IR,
  output [15:0] CYC,
  output halt,
  output [7:0] PC,
  output [7:0] IFID_PC,
  output IFID_V,
  output [7:0] IDEX_PC,
  output IDEX_V,
  output [7:0] EXMEM_PC,
  output EXMEM_V,
  output [7:0] MEMWB_PC,
  output MEMWB_V,
  output STALL,
  output FLUSH,
  output HALTED,
  output [1:0] FWD_A,
  output [1:0] FWD_B,
  output WB_WE,
  output [2:0] WB_RD,
  output [7:0] WB_DATA,
  output D_WE,
  output [7:0] D_ADDR,
  output [7:0] D_WDATA,
  output RAM_WE,
  output [7:0] ACT,
  output [7:0] DISP,
  output MOTOR_ACT,
  output TRIP,
  output [7:0] T_COUNT,
  output T_MATCH,
  output T_EN,
  output [7:0] T_LIMIT,
  output START,
  output DOOR,
  output [1:0] MODE,
  output [7:0] WL,
  output [7:0] RPM
);

  wire CLK, CYC_C, D_RE, EQHI, EQLO, PLANT_TICK, POR, RPM_NB, RST, WL_NB;
  wire [6:0] RAM_A;
  wire [7:0] CYC_HI_N, CYC_LO_N, D_RDATA, RAM_DO, RPM_DN, RPM_DNS, RPM_N, WL_DN, WL_DNS, WL_M1, WL_N, WL_UP;
  wire [15:0] I_DATA;
  wire [15:4] STIM;

  Clock #(.highDuration(1), .lowDuration(1)) u_CLK (.out(CLK));
  Register #(.width(1), .trigger("rising")) u_POR (.D(1'b1), .Q(POR), .clk(CLK));  // open: en, clr
  not not_1 (RST, POR);
  inc8 CNT_LO (.A(CYC[7:0]), .CI(1'b1), .S(CYC_LO_N), .CO(CYC_C));
  inc8 CNT_HI (.A(CYC[15:8]), .CI(CYC_C), .S(CYC_HI_N));  // open: CO
  eq8 eq8_1 (.A(CYC[7:0]), .B(8'h10), .EQ(EQLO));
  eq8 eq8_2 (.A(CYC[15:8]), .B(8'he), .EQ(EQHI));
  Register #(.width(8), .trigger("rising")) CYC_LO (.D(CYC_LO_N), .Q(CYC[7:0]), .clk(CLK));  // open: en, clr
  Register #(.width(8), .trigger("rising")) CYC_HI (.D(CYC_HI_N), .Q(CYC[15:8]), .clk(CLK));  // open: en, clr
  and and_1 (halt, EQLO, EQHI);
  ROM #(.addrWidth(8), .dataWidth(16)) rom_1 (.addr(CYC[11:4]), .data({STIM, MODE, DOOR, START}));  // open: sel
  add8 WL_3 (.A(WL), .B(8'h3), .CI(1'b0), .S(WL_UP));  // open: CO
  add8 WL_7 (.A(WL), .B(8'hf9), .CI(1'b0), .S(WL_DN), .CO(WL_NB));
  and8en and8en_1 (.D(WL_DN), .E(WL_NB), .Y(WL_DNS));
  add8 RPM_40 (.A(RPM), .B(8'hd8), .CI(1'b0), .S(RPM_DN), .CO(RPM_NB));
  and8en and8en_2 (.D(RPM_DN), .E(RPM_NB), .Y(RPM_DNS));
  mux2_8 mux2_8_1 (.D0(WL), .D1(WL_DNS), .S(ACT[3]), .Y(WL_M1));
  mux2_8 mux2_8_2 (.D0(WL_M1), .D1(WL_UP), .S(ACT[0]), .Y(WL_N));
  mux2_8 mux2_8_3 (.D0(RPM_DNS), .D1(8'hc8), .S(MOTOR_ACT), .Y(RPM_N));
  Register #(.width(8), .trigger("rising")) DRUM (.D(RPM_N), .Q(RPM), .clk(CLK));  // open: en, clr
  and and_2 (PLANT_TICK, CYC[0], CYC[1], CYC[2], CYC[3]);
  Register #(.width(8), .trigger("rising")) WATER (.D(WL_N), .en(PLANT_TICK), .Q(WL), .clk(CLK));  // open: clr
  cpu CPU (
    .CLK(CLK), .RST(RST), .I_DATA(I_DATA), .D_RDATA(D_RDATA), .I_ADDR(PC), .D_ADDR(D_ADDR),
    .D_WDATA(D_WDATA), .D_WE(D_WE), .D_RE(D_RE), .IFID_PC(IFID_PC), .IFID_V(IFID_V), .IFID_IR(IFID_IR),
    .IDEX_PC(IDEX_PC), .IDEX_V(IDEX_V), .EXMEM_PC(EXMEM_PC), .EXMEM_V(EXMEM_V), .MEMWB_PC(MEMWB_PC),
    .MEMWB_V(MEMWB_V), .STALL(STALL), .FLUSH(FLUSH), .HALTED(HALTED), .FWD_A(FWD_A), .FWD_B(FWD_B),
    .WB_WE(WB_WE), .WB_RD(WB_RD), .WB_DATA(WB_DATA));
  mmio MMIO (
    .CLK(CLK), .RST(RST), .ADDR(D_ADDR), .WDATA(D_WDATA), .WE(D_WE), .RAM_DO(RAM_DO), .START(START),
    .DOOR(DOOR), .MODE(MODE), .WL(WL), .TEMP(8'h19), .RPM(RPM), .RDATA(D_RDATA), .RAM_WE(RAM_WE),
    .RAM_A(RAM_A), .ACT(ACT), .DISP(DISP), .MOTOR_ACT(MOTOR_ACT), .TRIP(TRIP), .T_COUNT(T_COUNT),
    .T_MATCH(T_MATCH), .T_EN(T_EN), .T_LIMIT(T_LIMIT));
  ROM #(.addrWidth(8), .dataWidth(16)) rom_2 (.addr(PC), .data(I_DATA));  // open: sel
  RAM #(.addrWidth(7), .dataWidth(8), .bus("separate")) ram_1 (
    .addr(RAM_A), .din(D_WDATA), .data(RAM_DO), .str(RAM_WE), .clk(CLK));  // open: sel, ld, clr

  // Other names for the same wires on the sheet: VALVE_IN = ACT[0]; HEATER = ACT[1]; MOTOR_EN = ACT[2];
  //   PUMP_OUT = ACT[3]; MOTOR_DIR = ACT[4]; DOOR_LOCK = ACT[5]; BUZZER = ACT[6]; cy0 = CYC[0];
  //   CYC_LO[7:0] = CYC[7:0]; cy1 = CYC[1]; cy2 = CYC[2]; cy3 = CYC[3]; SADDR[7:0] = CYC[11:4];
  //   CYC_HI[7:0] = CYC[15:8]; HALT_TB = halt; STIM[3:0] = {MODE, DOOR, START}

  // Notes on the sheet:
  //   Test bench (auto power-on reset, scripted inputs, plant model)
  //   cycle counter
  //   stimulus ROM
  //   halt after N cycles
  //   contents of rom_1 (hex, n*v repeats v):
  //   2 2 3 3 3 3 3 3 2 2 2 2 2 2 2 2 2 2 2 2 2 2 2 2 2 2 2 2 2 2 6 6 6 6 6 6 6 6 6 6 6 6 6 6 6 6 6 6 6 6
  //   6 6 6 6 6 6 6 6 6 6 6 6 6 6 6 6 6 6 6 6 6 6 6 6 6 6 6 6 6 6 6 6 6 6 6 6 6 6 6 6 6 6 6 6 6 6 6 6 6 6
  //   7 7 7 7 7 7 6 6 6 6 6 6 6 6 6 6 6 6 6 6 6 6 6 6 6 6 6 6 6 6 6 6 6 6 6 6 6 6 6 6 6 6 6 6 6 6 6 6 6 6
  //   2 2 2 2 2 2 2 2 2 2 2 2 2 2 2 2 2 2 2 2 2 2 2 2 2 2 2 2 2 2 2 2 2 2 2 2 2 2 2 2 2 2 2 2 2 2 2 2 2 2
  //   2 2 2 2 2 2 2 2 2 2 2 2 2 2 2 2 2 2 2 2 2 2 2 2 2 2 2 2 2 2 2 2 2 2 2 2 2 2 2 2 2 2 2 2 2 2 2 2 2 2
  //   2 2 2 2 2 2
  //   plant model
  //   Processor (5-stage pipeline)
  //   Instruction ROM 256x16
  //   Data RAM 128x8 (0x00-0x7F)
  //   Memory-mapped I/O, timer, safety
  //   contents of rom_2 (hex, n*v repeats v):
  //   1000 1ef4 71c0 1efa 1202 73c0 1ef5 1201 73c0 1ef0 63c0 1403 5440 84fd a40a 160c 5640 36c0 36c0 1e04
  //   77c0 1404 5440 a41c 1864 1a40 1c20 b01f 18a0 1a60 1c30 1e00 79c0 8e01 7bc0 8e01 7dc0 8e01 180a 79c0
  //   1cf4 1220 7380 1ef5 22c0 8202 73c0 1ef0 63c0 1402 5440 94a0 1221 7380 1ef5 22c0 8203 73c0 1e00 69c0
  //   1ef1 63c0 c300 923d 1220 7380 1ef5 22c0 8204 73c0 1ef2 63c0 1e05 73c0 1e01 6bc0 1ef9 7bc0 1efa 1203
  //   73c0 10f0 1410 1624 1810 1af8 1efb 6340 5280 32c0 7380 6200 5300 a2a6 63c0 9257 1220 7380 1228 7380
  //   1e04 63c0 8205 1ef5 73c0 1e03 69c0 1ef1 63c0 2500 c440 946c 1e04 63c0 8206 1ef5 73c0 1e02 6bc0 1ef9
  //   7bc0 1efa 1203 73c0 122c 7380 10f0 1810 1efb 6200 5300 a2a6 63c0 9281 1220 7380 1efa 1202 73c0 1e04
  //   63c0 8207 1ef5 73c0 1ef3 63c0 a291 1240 7380 1e04 63c0 8208 1ef5 73c0 1ef0 63c0 1401 5440 a49b b009
  //   1200 7380 1ef5 12e1 73c0 b09a 1200 7380 1efa 1202 73c0 1ef5 12ee 73c0 1ef0 1810 63c0 5300 a2b0 b009
  //   monitored outputs (tty column order)
endmodule

module cpu (
  input  CLK,
  input  RST,
  input  [15:0] I_DATA,
  input  [7:0] D_RDATA,
  output [7:0] I_ADDR,
  output [7:0] D_ADDR,
  output [7:0] D_WDATA,
  output D_WE,
  output D_RE,
  output [7:0] IFID_PC,
  output IFID_V,
  output [15:0] IFID_IR,
  output [7:0] IDEX_PC,
  output IDEX_V,
  output [7:0] EXMEM_PC,
  output EXMEM_V,
  output [7:0] MEMWB_PC,
  output MEMWB_V,
  output STALL,
  output FLUSH,
  output HALTED,
  output [1:0] FWD_A,
  output [1:0] FWD_B,
  output WB_WE,
  output [2:0] WB_RD,
  output [7:0] WB_DATA
);

  wire HALT_EX, HOLD, IDV_D, IFID_EN, IFV_D, MEMWB_RW, NFLUSH, NHOLD, NSTALL, NZA, PC_EN, REDIRECT,
       STALL_RAW, TAKE, TBNZ, TBZ, USE_A, USE_B, ZA;
  wire [2:0] EXMEM_C, EXMEM_RD, IDEX_RA, IDEX_RB;
  wire [7:0] ALUR, ALUY, DA, DB, IDEX_DA, IDEX_DB, IDEX_IMM, MRES, NPC, OA0, OB0, OPA, OPB, PCP1;
  wire [12:0] CW, IDEX_CW;

  inc8 PC_1 (.A(I_ADDR), .CI(1'b1), .S(PCP1));  // open: CO
  mux2_8 NPC_MUX (.D0(PCP1), .D1(IDEX_IMM), .S(REDIRECT), .Y(NPC));
  not not_1 (NHOLD, HOLD);
  or or_1 (PC_EN, REDIRECT, NHOLD);
  or or_2 (FLUSH, REDIRECT, HALT_EX);
  not not_2 (NSTALL, STALL_RAW);
  or or_3 (IFID_EN, NSTALL, FLUSH);
  nor nor_1 (IFV_D, FLUSH, HALTED);
  Register #(.width(8), .trigger("rising")) PC (.D(NPC), .en(PC_EN), .Q(I_ADDR), .clk(CLK), .clr(RST));
  or or_4 (HOLD, STALL_RAW, HALT_EX, HALTED);
  Register #(.width(16), .trigger("rising")) u_IFID_IR (.D(I_DATA), .en(IFID_EN), .Q(IFID_IR), .clk(CLK), .clr(RST));
  Register #(.width(8), .trigger("rising")) u_IFID_PC (.D(I_ADDR), .en(IFID_EN), .Q(IFID_PC), .clk(CLK), .clr(RST));
  Register #(.width(1), .trigger("rising")) u_IFID_V (.D(IFV_D), .en(IFID_EN), .Q(IFID_V), .clk(CLK), .clr(RST));
  Register #(.width(1), .trigger("rising")) u_HALTED (.D(1'b1), .en(HALT_EX), .Q(HALTED), .clk(CLK), .clr(RST));
  control CONTROL (.OP(IFID_IR[15:12]), .CW(CW));
  regfile REGFILE (
    .RA(IFID_IR[11:9]), .RB(IFID_IR[8:6]), .WA(WB_RD), .WD(WB_DATA), .WE(WB_WE), .CLK(CLK), .DA(DA), .DB(DB));
  hazard HAZARD (
    .IFID_V(IFID_V), .UA(CW[3]), .UB(CW[4]), .RA(IFID_IR[11:9]), .RB(IFID_IR[8:6]), .IDEX_V(IDEX_V),
    .IDEX_MR(IDEX_CW[1]), .IDEX_RD(IDEX_RA), .STALL(STALL_RAW));
  not not_3 (NFLUSH, FLUSH);
  and and_1 (IDV_D, IFID_V, NSTALL, NFLUSH);
  and and_2 (STALL, STALL_RAW, NFLUSH);
  Register #(.width(1), .trigger("rising")) u_IDEX_V (.D(IDV_D), .Q(IDEX_V), .clk(CLK), .clr(RST));  // open: en
  Register #(.width(13), .trigger("rising")) u_IDEX_CW (.D(CW), .Q(IDEX_CW), .clk(CLK), .clr(RST));  // open: en
  Register #(.width(3), .trigger("rising")) u_IDEX_RA (
    .D(IFID_IR[11:9]), .Q(IDEX_RA), .clk(CLK), .clr(RST));  // open: en
  Register #(.width(3), .trigger("rising")) u_IDEX_RB (
    .D(IFID_IR[8:6]), .Q(IDEX_RB), .clk(CLK), .clr(RST));  // open: en
  Register #(.width(8), .trigger("rising")) u_IDEX_DA (.D(DA), .Q(IDEX_DA), .clk(CLK), .clr(RST));  // open: en
  Register #(.width(8), .trigger("rising")) u_IDEX_DB (.D(DB), .Q(IDEX_DB), .clk(CLK), .clr(RST));  // open: en
  Register #(.width(8), .trigger("rising")) u_IDEX_IMM (
    .D(IFID_IR[7:0]), .Q(IDEX_IMM), .clk(CLK), .clr(RST));  // open: en
  Register #(.width(8), .trigger("rising")) u_IDEX_PC (.D(IFID_PC), .Q(IDEX_PC), .clk(CLK), .clr(RST));  // open: en
  fwd u_FWD_A (
    .SRC(IDEX_RA), .USE(USE_A), .EXMEM_V(EXMEM_V), .EXMEM_RW(EXMEM_C[0]), .EXMEM_MR(EXMEM_C[1]),
    .EXMEM_RD(EXMEM_RD), .MEMWB_V(MEMWB_V), .MEMWB_RW(MEMWB_RW), .MEMWB_RD(WB_RD), .F_EXMEM(FWD_A[1]),
    .F_MEMWB(FWD_A[0]));
  fwd u_FWD_B (
    .SRC(IDEX_RB), .USE(USE_B), .EXMEM_V(EXMEM_V), .EXMEM_RW(EXMEM_C[0]), .EXMEM_MR(EXMEM_C[1]),
    .EXMEM_RD(EXMEM_RD), .MEMWB_V(MEMWB_V), .MEMWB_RW(MEMWB_RW), .MEMWB_RD(WB_RD), .F_EXMEM(FWD_B[1]),
    .F_MEMWB(FWD_B[0]));
  mux2_8 FA_M1 (.D0(IDEX_DA), .D1(WB_DATA), .S(FWD_A[0]), .Y(OA0));
  mux2_8 FA_M2 (.D0(OA0), .D1(D_ADDR), .S(FWD_A[1]), .Y(OPA));
  mux2_8 FB_M1 (.D0(IDEX_DB), .D1(WB_DATA), .S(FWD_B[0]), .Y(OB0));
  mux2_8 FB_M2 (.D0(OB0), .D1(D_ADDR), .S(FWD_B[1]), .Y(OPB));
  and and_3 (USE_A, IDEX_V, IDEX_CW[3]);
  and and_4 (USE_B, IDEX_V, IDEX_CW[4]);
  alu8 ALU (.X(OPA), .Y(ALUY), .OP(IDEX_CW[7:6]), .SUB(IDEX_CW[8]), .R(ALUR));  // open: CO
  zero8 ZERO (.A(OPA), .Z(ZA));
  not not_4 (NZA, ZA);
  mux2_8 YSEL (.D0(OPB), .D1(IDEX_IMM), .S(IDEX_CW[5]), .Y(ALUY));
  and and_5 (TBZ, IDEX_CW[9], ZA);
  and and_6 (TBNZ, IDEX_CW[10], NZA);
  or or_5 (TAKE, IDEX_CW[11], TBZ, TBNZ);
  and and_7 (REDIRECT, IDEX_V, TAKE);
  and and_8 (HALT_EX, IDEX_V, IDEX_CW[12]);
  Register #(.width(1), .trigger("rising")) u_EXMEM_V (.D(IDEX_V), .Q(EXMEM_V), .clk(CLK), .clr(RST));  // open: en
  Register #(.width(3), .trigger("rising")) EXMEM_CTRL (
    .D(IDEX_CW[2:0]), .Q(EXMEM_C), .clk(CLK), .clr(RST));  // open: en
  Register #(.width(8), .trigger("rising")) EXMEM_ALU (.D(ALUR), .Q(D_ADDR), .clk(CLK), .clr(RST));  // open: en
  Register #(.width(8), .trigger("rising")) EXMEM_SDATA (.D(OPA), .Q(D_WDATA), .clk(CLK), .clr(RST));  // open: en
  Register #(.width(3), .trigger("rising")) u_EXMEM_RD (.D(IDEX_RA), .Q(EXMEM_RD), .clk(CLK), .clr(RST));  // open: en
  Register #(.width(8), .trigger("rising")) u_EXMEM_PC (.D(IDEX_PC), .Q(EXMEM_PC), .clk(CLK), .clr(RST));  // open: en
  mux2_8 LOAD_MUX (.D0(D_ADDR), .D1(D_RDATA), .S(EXMEM_C[1]), .Y(MRES));
  Register #(.width(8), .trigger("rising")) MEMWB_RES (.D(MRES), .Q(WB_DATA), .clk(CLK), .clr(RST));  // open: en
  and and_9 (D_WE, EXMEM_V, EXMEM_C[2]);
  and and_10 (D_RE, EXMEM_V, EXMEM_C[1]);
  Register #(.width(1), .trigger("rising")) u_MEMWB_V (.D(EXMEM_V), .Q(MEMWB_V), .clk(CLK), .clr(RST));  // open: en
  Register #(.width(1), .trigger("rising")) u_MEMWB_RW (
    .D(EXMEM_C[0]), .Q(MEMWB_RW), .clk(CLK), .clr(RST));  // open: en
  Register #(.width(3), .trigger("rising")) MEMWB_RD (.D(EXMEM_RD), .Q(WB_RD), .clk(CLK), .clr(RST));  // open: en
  Register #(.width(8), .trigger("rising")) u_MEMWB_PC (.D(EXMEM_PC), .Q(MEMWB_PC), .clk(CLK), .clr(RST));  // open: en
  and and_11 (WB_WE, MEMWB_V, MEMWB_RW);

  // Other names for the same wires on the sheet: ID_UA = CW[3]; ID_UB = CW[4]; EXMEM_ALU[7:0] = D_ADDR;
  //   EXMEM_RW = EXMEM_C[0]; EXMEM_MR = EXMEM_C[1]; EXMEM_MW = EXMEM_C[2]; EXMEM_SD[7:0] = D_WDATA;
  //   FA_MEMWB = FWD_A[0]; FWDA[1:0] = FWD_A; FA_EXMEM = FWD_A[1]; FB_MEMWB = FWD_B[0]; FWDB[1:0] = FWD_B;
  //   FB_EXMEM = FWD_B[1]; X_UA = IDEX_CW[3]; X_UB = IDEX_CW[4]; X_YI = IDEX_CW[5]; X_AOP[1:0] = IDEX_CW[7:6];
  //   X_SB = IDEX_CW[8]; X_BZ = IDEX_CW[9]; X_BNZ = IDEX_CW[10]; X_JP = IDEX_CW[11]; X_HT = IDEX_CW[12];
  //   IMM[7:0] = IFID_IR[7:0]; RB[2:0] = IFID_IR[8:6]; RA[2:0] = IFID_IR[11:9]; OPC[3:0] = IFID_IR[15:12];
  //   MEMWB_RD[2:0] = WB_RD; MEMWB_RES[7:0] = WB_DATA; PC[7:0] = I_ADDR; X_RW = IDEX_CW[0]; XC3[2:0] = IDEX_CW[2:0];
  //   X_MR = IDEX_CW[1]; X_MW = IDEX_CW[2]

  // Notes on the sheet:
  //   IF: PC / next-PC / IF-ID
  //   ID: decode / register read / hazard
  //   ID/EX pipeline register
  //   EX: forwarding / ALU / branch
  //   EX/MEM pipeline register
  //   MEM: data port / MEM-WB
  //   WB
endmodule

module mmio (
  input  CLK,
  input  RST,
  input  [7:0] ADDR,
  input  [7:0] WDATA,
  input  WE,
  input  [7:0] RAM_DO,
  input  START,
  input  DOOR,
  input  [1:0] MODE,
  input  [7:0] WL,
  input  [7:0] TEMP,
  input  [7:0] RPM,
  output [7:0] RDATA,
  output RAM_WE,
  output [6:0] RAM_A,
  output [7:0] ACT,
  output [7:0] DISP,
  output MOTOR_ACT,
  output TRIP,
  output [7:0] T_COUNT,
  output T_MATCH,
  output T_EN,
  output [7:0] T_LIMIT
);

  wire IS_PER, IS_RAM, p0, p1, p2, p3, p4, p5, p8, p9, p10, p11, SEL_F0, SEL_F1, SEL_F2, SEL_F3, SEL_F4,
       SEL_F5, SEL_F8, SEL_F9, SEL_FA, SEL_FB, WE_ACT, WE_CTRL, WE_DISP, WE_LIMIT;
  wire [7:0] RD0, RD1, RD2, RD3, RD4, RD5, RD6, RD7, RD8, RD9, RD10, WACT;
  wire [15:6] PSEL;

  dec4to16 PDEC (.A(ADDR[3:0]), .Y({PSEL[15:12], p11, p10, p9, p8, PSEL[7:6], p5, p4, p3, p2, p1, p0}));
  not not_1 (IS_RAM, ADDR[7]);
  and and_1 (IS_PER, ADDR[4], ADDR[5], ADDR[6], ADDR[7]);
  and and_2 (SEL_F0, IS_PER, p0);
  and and_3 (SEL_F1, IS_PER, p1);
  and and_4 (SEL_F2, IS_PER, p2);
  and and_5 (SEL_F3, IS_PER, p3);
  and and_6 (SEL_F4, IS_PER, p4);
  and and_7 (SEL_F5, IS_PER, p5);
  and and_8 (SEL_F8, IS_PER, p8);
  and and_9 (SEL_F9, IS_PER, p9);
  and and_10 (SEL_FA, IS_PER, p10);
  and and_11 (SEL_FB, IS_PER, p11);
  and and_12 (RAM_WE, WE, IS_RAM);
  and and_13 (WE_ACT, WE, SEL_F4);
  and and_14 (WE_DISP, WE, SEL_F5);
  and and_15 (WE_LIMIT, WE, SEL_F9);
  and and_16 (WE_CTRL, WE, SEL_FA);
  timer8 TIMER (
    .CLK(CLK), .RST(RST), .WD(WDATA), .WE_LIMIT(WE_LIMIT), .WE_CTRL(WE_CTRL), .COUNT(T_COUNT),
    .LIMIT(T_LIMIT), .EN(T_EN), .MATCH(T_MATCH));
  safety SAFETY (
    .CLK(CLK), .RST(RST), .REQ(ACT[2]), .DOOR(DOOR), .START(START), .ACTUAL(MOTOR_ACT), .TRIP(TRIP));  // open: RISE
  assign WACT = WDATA & 8'h7f;  // AND_Gate and_17, 8 bits wide
  Register #(.width(8), .trigger("rising")) ACT_LATCH (.D(WACT), .en(WE_ACT), .Q(ACT), .clk(CLK), .clr(RST));
  Register #(.width(8), .trigger("rising")) DISPLAY (.D(WDATA), .en(WE_DISP), .Q(DISP), .clk(CLK), .clr(RST));
  and8en and8en_1 (.D(RAM_DO), .E(IS_RAM), .Y(RD0));
  and8en and8en_2 (.D({2'b00, MOTOR_ACT, TRIP, MODE, DOOR, START}), .E(SEL_F0), .Y(RD1));
  and8en and8en_3 (.D(WL), .E(SEL_F1), .Y(RD2));
  and8en and8en_4 (.D(TEMP), .E(SEL_F2), .Y(RD3));
  and8en and8en_5 (.D(RPM), .E(SEL_F3), .Y(RD4));
  and8en and8en_6 (.D(ACT), .E(SEL_F4), .Y(RD5));
  and8en and8en_7 (.D(DISP), .E(SEL_F5), .Y(RD6));
  and8en and8en_8 (.D(T_COUNT), .E(SEL_F8), .Y(RD7));
  and8en and8en_9 (.D(T_LIMIT), .E(SEL_F9), .Y(RD8));
  and8en and8en_10 (.D({{7{1'b0}}, T_EN}), .E(SEL_FA), .Y(RD9));
  and8en and8en_11 (.D({{7{1'b0}}, T_MATCH}), .E(SEL_FB), .Y(RD10));
  assign RDATA = RD0 | RD1 | RD2 | RD3 | RD4 | RD5 | RD6 | RD7 | RD8 | RD9 | RD10;  // OR_Gate or_1, 8 bits wide

  assign RAM_A = ADDR[6:0];

  // Other names for the same wires on the sheet: MOTOR_REQ = ACT[2]; LO[3:0] = ADDR[3:0]; A4 = ADDR[4]; A5 = ADDR[5];
  //   A6 = ADDR[6]; A7 = ADDR[7]; A7b = ADDR[7]; CTRL_RB[0] = T_EN;
  //   PSEL (some bits) = {p11, p10, p9, p8, p5, p4, p3, p2, p1, p0};
  //   STATUS[5:0] = {MOTOR_ACT, TRIP, MODE, DOOR, START}; TSTAT[0] = T_MATCH

  // Notes on the sheet:
  //   address decode
  //   selects / write enables
  //   output latches
  //   timer / safety
  //   read-back words
  //   read mux (AND-OR)
endmodule

module regfile (
  input  [2:0] RA,
  input  [2:0] RB,
  input  [2:0] WA,
  input  [7:0] WD,
  input  WE,
  input  CLK,
  output [7:0] DA,
  output [7:0] DB
);

  wire BPA, BPB, EQA, EQB, we0, we1, we2, we3, we4, we5, we6, we7, ws0, ws1, ws2, ws3, ws4, ws5, ws6, ws7;
  wire [7:0] R0, R1, R2, R3, R4, R5, R6, R7, RDA, RDB;

  dec3to8 WDEC (.A(WA), .Y({ws7, ws6, ws5, ws4, ws3, ws2, ws1, ws0}));
  and and_1 (we0, WE, ws0);
  and and_2 (we1, WE, ws1);
  and and_3 (we2, WE, ws2);
  and and_4 (we3, WE, ws3);
  and and_5 (we4, WE, ws4);
  and and_6 (we5, WE, ws5);
  and and_7 (we6, WE, ws6);
  and and_8 (we7, WE, ws7);
  Register #(.width(8), .trigger("rising")) u_R0 (.D(WD), .en(we0), .Q(R0), .clk(CLK));  // open: clr
  Register #(.width(8), .trigger("rising")) u_R1 (.D(WD), .en(we1), .Q(R1), .clk(CLK));  // open: clr
  Register #(.width(8), .trigger("rising")) u_R2 (.D(WD), .en(we2), .Q(R2), .clk(CLK));  // open: clr
  Register #(.width(8), .trigger("rising")) u_R3 (.D(WD), .en(we3), .Q(R3), .clk(CLK));  // open: clr
  Register #(.width(8), .trigger("rising")) u_R4 (.D(WD), .en(we4), .Q(R4), .clk(CLK));  // open: clr
  Register #(.width(8), .trigger("rising")) u_R5 (.D(WD), .en(we5), .Q(R5), .clk(CLK));  // open: clr
  Register #(.width(8), .trigger("rising")) u_R6 (.D(WD), .en(we6), .Q(R6), .clk(CLK));  // open: clr
  Register #(.width(8), .trigger("rising")) u_R7 (.D(WD), .en(we7), .Q(R7), .clk(CLK));  // open: clr
  mux8_8 READ_A (.D0(R0), .D1(R1), .D2(R2), .D3(R3), .D4(R4), .D5(R5), .D6(R6), .D7(R7), .S(RA), .Y(RDA));
  mux8_8 READ_B (.D0(R0), .D1(R1), .D2(R2), .D3(R3), .D4(R4), .D5(R5), .D6(R6), .D7(R7), .S(RB), .Y(RDB));
  eq3 eq3_1 (.A(WA), .B(RA), .EQ(EQA));
  mux2_8 BYP_A (.D0(RDA), .D1(WD), .S(BPA), .Y(DA));
  eq3 eq3_2 (.A(WA), .B(RB), .EQ(EQB));
  mux2_8 BYP_B (.D0(RDB), .D1(WD), .S(BPB), .Y(DB));
  and and_9 (BPA, WE, EQA);
  and and_10 (BPB, WE, EQB);

  // Other names for the same wires on the sheet: WSEL[7:0] = {ws7, ws6, ws5, ws4, ws3, ws2, ws1, ws0}

  // Notes on the sheet:
  //   write decode
  //   R0..R7
  //   read ports
  //   WB->ID bypass
endmodule

module control (
  input  [3:0] OP,
  output [12:0] CW
);

  wire is_ADD, is_ADDI, is_AND, is_LDI, is_MOV, is_NOP, is_RSV_D, is_RSV_E, is_SGEU, is_SUB;

  dec4to16 OPDEC (
    .A(OP),
    .Y({CW[12], is_RSV_E, is_RSV_D, is_SGEU, CW[11:9], is_ADDI, CW[2:1], is_AND, is_SUB, is_ADD, is_MOV, is_LDI, is_NOP}));
  or or_1 (CW[5], is_LDI, is_ADDI);
  or or_2 (CW[6], is_AND, is_SGEU);
  or or_3 (CW[8], is_SUB, is_SGEU);
  or or_4 (CW[0], is_LDI, is_MOV, is_ADD, is_SUB, is_AND, CW[1], is_ADDI, is_SGEU);
  or or_5 (CW[3], is_ADD, is_SUB, is_AND, CW[2], is_ADDI, CW[9], CW[10], is_SGEU);
  or or_6 (CW[4], is_MOV, is_ADD, is_SUB, is_AND, CW[1], CW[2], is_SGEU);
  or or_7 (CW[7], is_LDI, is_MOV, CW[1], CW[2], is_SGEU);

  // Other names for the same wires on the sheet: RW = CW[0]; is_LD = CW[1];
  //   OH[15:0] = {CW[12], is_RSV_E, is_RSV_D, is_SGEU, CW[11:9], is_ADDI, CW[2:1], is_AND, is_SUB, is_ADD, is_MOV, is_LDI, is_NOP};
  //   is_ST = CW[2]; UA = CW[3]; UB = CW[4]; YI = CW[5]; AOP0 = CW[6]; AOP1 = CW[7]; SB = CW[8]; is_BEQZ = CW[9];
  //   is_BNEZ = CW[10]; is_JMP = CW[11]; is_HALT = CW[12]
endmodule

module hazard (
  input  IFID_V,
  input  UA,
  input  UB,
  input  [2:0] RA,
  input  [2:0] RB,
  input  IDEX_V,
  input  IDEX_MR,
  input  [2:0] IDEX_RD,
  output STALL
);

  wire EA, EB, HA, HAB, HB;

  eq3 eq3_1 (.A(RA), .B(IDEX_RD), .EQ(EA));
  eq3 eq3_2 (.A(RB), .B(IDEX_RD), .EQ(EB));
  and and_1 (HA, UA, EA);
  and and_2 (HB, UB, EB);
  or or_1 (HAB, HA, HB);
  and and_3 (STALL, IFID_V, IDEX_V, IDEX_MR, HAB);
endmodule

module fwd (
  input  [2:0] SRC,
  input  USE,
  input  EXMEM_V,
  input  EXMEM_RW,
  input  EXMEM_MR,
  input  [2:0] EXMEM_RD,
  input  MEMWB_V,
  input  MEMWB_RW,
  input  [2:0] MEMWB_RD,
  output F_EXMEM,
  output F_MEMWB
);

  wire E1, E2, EXM, M2, NEXM, NMR;

  eq3 eq3_1 (.A(EXMEM_RD), .B(SRC), .EQ(E1));
  and and_1 (F_EXMEM, EXM, NMR);
  eq3 eq3_2 (.A(MEMWB_RD), .B(SRC), .EQ(E2));
  not not_1 (NEXM, EXM);
  and and_2 (F_MEMWB, M2, NEXM);
  not not_2 (NMR, EXMEM_MR);
  and and_3 (EXM, USE, EXMEM_V, EXMEM_RW, E1);
  and and_4 (M2, USE, MEMWB_V, MEMWB_RW, E2);
endmodule

module alu8 (
  input  [7:0] X,
  input  [7:0] Y,
  input  [1:0] OP,
  input  SUB,
  output [7:0] R,
  output CO
);

  wire [7:0] ANDV, SUM, YX;

  assign YX = Y ^ {8{SUB}};  // XOR_Gate xor_1, 8 bits wide
  add8 ADDER (.A(X), .B(YX), .CI(SUB), .S(SUM), .CO(CO));
  assign ANDV = X & Y;  // AND_Gate and_1, 8 bits wide
  mux4_8 RESULT_MUX (.D0(SUM), .D1(ANDV), .D2(Y), .D3({{7{1'b0}}, CO}), .S(OP), .Y(R));

  // Other names for the same wires on the sheet: SGE[0] = CO; SUB8[7:0] = {8{SUB}}
endmodule

module timer8 (
  input  CLK,
  input  RST,
  input  [7:0] WD,
  input  WE_LIMIT,
  input  WE_CTRL,
  output [7:0] COUNT,
  output [7:0] LIMIT,
  output EN,
  output MATCH
);

  wire CLRCMD, CNT_EN, EQL, HIT, LNZ, LZ, M_D, MH, NCLR;
  wire [7:0] CNT_D, INC;

  Register #(.width(1), .trigger("rising")) u_EN (.D(WD[0]), .en(WE_CTRL), .Q(EN), .clk(CLK), .clr(RST));
  and and_1 (CLRCMD, WE_CTRL, WD[1]);
  not not_1 (NCLR, CLRCMD);
  inc8 u_INC (.A(COUNT), .CI(1'b1), .S(INC));  // open: CO
  and8en and8en_1 (.D(INC), .E(NCLR), .Y(CNT_D));
  or or_1 (CNT_EN, CLRCMD, EN);
  Register #(.width(8), .trigger("rising")) u_COUNT (.D(CNT_D), .en(CNT_EN), .Q(COUNT), .clk(CLK), .clr(RST));
  eq8 eq8_1 (.A(INC), .B(LIMIT), .EQ(EQL));
  zero8 zero8_1 (.A(LIMIT), .Z(LZ));
  not not_2 (LNZ, LZ);
  Register #(.width(1), .trigger("rising")) u_MATCH (.D(M_D), .Q(MATCH), .clk(CLK), .clr(RST));  // open: en
  and and_2 (HIT, EN, EQL, LNZ);
  or or_2 (MH, MATCH, HIT);
  and and_3 (M_D, MH, NCLR);
  Register #(.width(8), .trigger("rising")) u_LIMIT (.D(WD), .en(WE_LIMIT), .Q(LIMIT), .clk(CLK), .clr(RST));

  // Notes on the sheet:
  //   CTRL: bit0 EN, bit1 CLR
  //   COUNT
  //   LIMIT / sticky MATCH
endmodule

module safety (
  input  CLK,
  input  RST,
  input  REQ,
  input  DOOR,
  input  START,
  output ACTUAL,
  output TRIP,
  output RISE
);

  wire HOLD, NDOOR, NREARM, NREQ, NSPREV, NTRIP, REARM, SET_TRIP, SPREV, TRIP_D;

  Register #(.width(1), .trigger("rising")) START_PREV (.D(START), .Q(SPREV), .clk(CLK), .clr(RST));  // open: en
  not not_1 (NSPREV, SPREV);
  and and_1 (RISE, START, NSPREV);
  not not_2 (NDOOR, DOOR);
  and and_2 (SET_TRIP, REQ, NDOOR);
  not not_3 (NREQ, REQ);
  and and_3 (REARM, NREQ, DOOR, RISE);
  not not_4 (NREARM, REARM);
  and and_4 (HOLD, TRIP, NREARM);
  or or_1 (TRIP_D, SET_TRIP, HOLD);
  Register #(.width(1), .trigger("rising")) u_TRIP (.D(TRIP_D), .Q(TRIP), .clk(CLK), .clr(RST));  // open: en
  not not_5 (NTRIP, TRIP);
  and and_5 (ACTUAL, REQ, DOOR, NTRIP);

  // Notes on the sheet:
  //   START edge detector
  //   TRIP latch
  //   combinational gate
endmodule

module add8 (
  input  [7:0] A,
  input  [7:0] B,
  input  CI,
  output [7:0] S,
  output CO
);

  wire c1, c2, c3, c4, c5, c6, c7;

  fa1 FA0 (.A(A[0]), .B(B[0]), .CI(CI), .S(S[0]), .CO(c1));
  fa1 FA1 (.A(A[1]), .B(B[1]), .CI(c1), .S(S[1]), .CO(c2));
  fa1 FA2 (.A(A[2]), .B(B[2]), .CI(c2), .S(S[2]), .CO(c3));
  fa1 FA3 (.A(A[3]), .B(B[3]), .CI(c3), .S(S[3]), .CO(c4));
  fa1 FA4 (.A(A[4]), .B(B[4]), .CI(c4), .S(S[4]), .CO(c5));
  fa1 FA5 (.A(A[5]), .B(B[5]), .CI(c5), .S(S[5]), .CO(c6));
  fa1 FA6 (.A(A[6]), .B(B[6]), .CI(c6), .S(S[6]), .CO(c7));
  fa1 FA7 (.A(A[7]), .B(B[7]), .CI(c7), .S(S[7]), .CO(CO));
endmodule

module inc8 (
  input  [7:0] A,
  input  CI,
  output [7:0] S,
  output CO
);

  wire c1, c2, c3, c4, c5, c6, c7;

  ha1 HA0 (.A(A[0]), .CI(CI), .S(S[0]), .CO(c1));
  ha1 HA1 (.A(A[1]), .CI(c1), .S(S[1]), .CO(c2));
  ha1 HA2 (.A(A[2]), .CI(c2), .S(S[2]), .CO(c3));
  ha1 HA3 (.A(A[3]), .CI(c3), .S(S[3]), .CO(c4));
  ha1 HA4 (.A(A[4]), .CI(c4), .S(S[4]), .CO(c5));
  ha1 HA5 (.A(A[5]), .CI(c5), .S(S[5]), .CO(c6));
  ha1 HA6 (.A(A[6]), .CI(c6), .S(S[6]), .CO(c7));
  ha1 HA7 (.A(A[7]), .CI(c7), .S(S[7]), .CO(CO));
endmodule

module fa1 (
  input  A,
  input  B,
  input  CI,
  output S,
  output CO
);

  wire G, P, T;

  xor xor_1 (P, A, B);
  xor xor_2 (S, P, CI);
  and and_1 (G, A, B);
  and and_2 (T, P, CI);
  or or_1 (CO, G, T);
endmodule

module ha1 (
  input  A,
  input  CI,
  output S,
  output CO
);

  xor xor_1 (S, A, CI);
  and and_1 (CO, A, CI);
endmodule

module mux2_8 (
  input  [7:0] D0,
  input  [7:0] D1,
  input  S,
  output [7:0] Y
);

  wire [7:0] NS8, T0, T1;

  assign NS8 = ~{8{S}};  // NOT_Gate not_1, 8 bits wide
  assign T1 = D1 & {8{S}};  // AND_Gate and_1, 8 bits wide
  assign T0 = D0 & NS8;  // AND_Gate and_2, 8 bits wide
  assign Y = T0 | T1;  // OR_Gate or_1, 8 bits wide

  // Other names for the same wires on the sheet: S8[7:0] = {8{S}}
endmodule

module mux4_8 (
  input  [7:0] D0,
  input  [7:0] D1,
  input  [7:0] D2,
  input  [7:0] D3,
  input  [1:0] S,
  output [7:0] Y
);

  wire [7:0] L0, L1;

  mux2_8 M0 (.D0(D0), .D1(D1), .S(S[0]), .Y(L0));
  mux2_8 M1 (.D0(D2), .D1(D3), .S(S[0]), .Y(L1));
  mux2_8 M2 (.D0(L0), .D1(L1), .S(S[1]), .Y(Y));
endmodule

module mux8_8 (
  input  [7:0] D0,
  input  [7:0] D1,
  input  [7:0] D2,
  input  [7:0] D3,
  input  [7:0] D4,
  input  [7:0] D5,
  input  [7:0] D6,
  input  [7:0] D7,
  input  [2:0] S,
  output [7:0] Y
);

  wire [7:0] L0, L1, L2, L3, M0, M1;

  mux2_8 A0 (.D0(D0), .D1(D1), .S(S[0]), .Y(L0));
  mux2_8 A1 (.D0(D2), .D1(D3), .S(S[0]), .Y(L1));
  mux2_8 A2 (.D0(D4), .D1(D5), .S(S[0]), .Y(L2));
  mux2_8 A3 (.D0(D6), .D1(D7), .S(S[0]), .Y(L3));
  mux2_8 B0 (.D0(L0), .D1(L1), .S(S[1]), .Y(M0));
  mux2_8 B1 (.D0(L2), .D1(L3), .S(S[1]), .Y(M1));
  mux2_8 C0 (.D0(M0), .D1(M1), .S(S[2]), .Y(Y));
endmodule

module and8en (
  input  [7:0] D,
  input  E,
  output [7:0] Y
);

  assign Y = D & {8{E}};  // AND_Gate and_1, 8 bits wide

  // Other names for the same wires on the sheet: E8[7:0] = {8{E}}
endmodule

module zero8 (
  input  [7:0] A,
  output Z
);

  nor nor_1 (Z, A[0], A[1], A[2], A[3], A[4], A[5], A[6], A[7]);
endmodule

module eq8 (
  input  [7:0] A,
  input  [7:0] B,
  output EQ
);

  wire [7:0] X;

  assign X = A ^ B;  // XOR_Gate xor_1, 8 bits wide
  nor nor_1 (EQ, X[0], X[1], X[2], X[3], X[4], X[5], X[6], X[7]);
endmodule

module eq3 (
  input  [2:0] A,
  input  [2:0] B,
  output EQ
);

  wire [2:0] X;

  assign X = A ^ B;  // XOR_Gate xor_1, 3 bits wide
  nor nor_1 (EQ, X[0], X[1], X[2]);
endmodule

module dec3to8 (
  input  [2:0] A,
  output [7:0] Y
);

  wire n0, n1, n2;

  not not_1 (n0, A[0]);
  not not_2 (n1, A[1]);
  not not_3 (n2, A[2]);
  and and_1 (Y[0], n0, n1, n2);
  and and_2 (Y[1], A[0], n1, n2);
  and and_3 (Y[2], n0, A[1], n2);
  and and_4 (Y[3], A[0], A[1], n2);
  and and_5 (Y[4], n0, n1, A[2]);
  and and_6 (Y[5], A[0], n1, A[2]);
  and and_7 (Y[6], n0, A[1], A[2]);
  and and_8 (Y[7], A[0], A[1], A[2]);
endmodule

module dec4to16 (
  input  [3:0] A,
  output [15:0] Y
);

  wire n0, n1, n2, n3;

  not not_1 (n0, A[0]);
  not not_2 (n1, A[1]);
  not not_3 (n2, A[2]);
  not not_4 (n3, A[3]);
  and and_1 (Y[0], n0, n1, n2, n3);
  and and_2 (Y[1], A[0], n1, n2, n3);
  and and_3 (Y[2], n0, A[1], n2, n3);
  and and_4 (Y[3], A[0], A[1], n2, n3);
  and and_5 (Y[4], n0, n1, A[2], n3);
  and and_6 (Y[5], A[0], n1, A[2], n3);
  and and_7 (Y[6], n0, A[1], A[2], n3);
  and and_8 (Y[7], A[0], A[1], A[2], n3);
  and and_9 (Y[8], n0, n1, n2, A[3]);
  and and_10 (Y[9], A[0], n1, n2, A[3]);
  and and_11 (Y[10], n0, A[1], n2, A[3]);
  and and_12 (Y[11], A[0], A[1], n2, A[3]);
  and and_13 (Y[12], n0, n1, A[2], A[3]);
  and and_14 (Y[13], A[0], n1, A[2], A[3]);
  and and_15 (Y[14], n0, A[1], A[2], A[3]);
  and and_16 (Y[15], A[0], A[1], A[2], A[3]);
endmodule
