// Logisim project washing_machine.circ as structural Verilog: 20 circuits, main circuit main
module FA (
  input  A,
  input  B,
  input  CI,
  output S,
  output CO
);

  wire t1, t2, t3, t4, t5;

  xor xor_1 (t1, A, B);
  xor xor_2 (t2, t1, CI);
  or or_1 (S, t2, t2);
  and and_1 (t3, A, B);
  and and_2 (t4, t1, CI);
  or or_2 (t5, t3, t4);
  or or_3 (CO, t5, t5);
endmodule

module ADD8 (
  input  [7:0] A,
  input  [7:0] B,
  input  CI,
  output [7:0] S,
  output CO
);

  wire t17, t18, t19, t20, t21, t22, t23, t24, t25, t26, t27, t28, t29, t30, t31, t32;

  FA fa_1 (.A(A[0]), .B(B[0]), .CI(CI), .S(t17), .CO(t18));
  FA fa_2 (.A(A[1]), .B(B[1]), .CI(t18), .S(t19), .CO(t20));
  FA fa_3 (.A(A[2]), .B(B[2]), .CI(t20), .S(t21), .CO(t22));
  FA fa_4 (.A(A[3]), .B(B[3]), .CI(t22), .S(t23), .CO(t24));
  FA fa_5 (.A(A[4]), .B(B[4]), .CI(t24), .S(t25), .CO(t26));
  FA fa_6 (.A(A[5]), .B(B[5]), .CI(t26), .S(t27), .CO(t28));
  FA fa_7 (.A(A[6]), .B(B[6]), .CI(t28), .S(t29), .CO(t30));
  FA fa_8 (.A(A[7]), .B(B[7]), .CI(t30), .S(t31), .CO(t32));
  assign S = {t31, t29, t27, t25, t23, t21, t19, t17} | {t31, t29, t27, t25, t23, t21, t19, t17};  // OR_Gate or_1, 8 bits wide
  or or_2 (CO, t32, t32);

  // Other names for the same wires on the sheet: t1 = A[0]; t2 = A[1]; t3 = A[2]; t4 = A[3]; t5 = A[4]; t6 = A[5];
  //   t7 = A[6]; t8 = A[7]; t9 = B[0]; t10 = B[1]; t11 = B[2]; t12 = B[3]; t13 = B[4]; t14 = B[5]; t15 = B[6];
  //   t16 = B[7]; t33[7:0] = {t31, t29, t27, t25, t23, t21, t19, t17}
endmodule

module INC8 (
  input  [7:0] A,
  output [7:0] S
);

  wire t2;
  wire [7:0] t1;

  ADD8 add8_1 (.A(A), .B({8{1'b0}}), .CI(1'b1), .S(t1), .CO(t2));
  assign S = t1 | t1;  // OR_Gate or_1, 8 bits wide
endmodule

module MUX2_8 (
  input  [7:0] A,
  input  [7:0] B,
  input  S,
  output [7:0] Y
);

  wire t1;
  wire [7:0] t3, t5, t6;

  not not_1 (t1, S);
  assign t3 = A & {8{t1}};  // AND_Gate and_1, 8 bits wide
  assign t5 = B & {8{S}};  // AND_Gate and_2, 8 bits wide
  assign t6 = t3 | t5;  // OR_Gate or_1, 8 bits wide
  assign Y = t6 | t6;  // OR_Gate or_2, 8 bits wide

  // Other names for the same wires on the sheet: t2[7:0] = {8{t1}}; t4[7:0] = {8{S}}
endmodule

module DEC3 (
  input  [2:0] A,
  output [7:0] Y
);

  wire t4, t5, t6, t7, t8, t9, t10, t11, t12, t13, t14;

  not not_1 (t4, A[0]);
  not not_2 (t5, A[1]);
  not not_3 (t6, A[2]);
  and and_1 (t7, t4, t5, t6);
  and and_2 (t8, A[0], t5, t6);
  and and_3 (t9, t4, A[1], t6);
  and and_4 (t10, A[0], A[1], t6);
  and and_5 (t11, t4, t5, A[2]);
  and and_6 (t12, A[0], t5, A[2]);
  and and_7 (t13, t4, A[1], A[2]);
  and and_8 (t14, A[0], A[1], A[2]);
  assign Y = {t14, t13, t12, t11, t10, t9, t8, t7} | {t14, t13, t12, t11, t10, t9, t8, t7};  // OR_Gate or_1, 8 bits wide

  // Other names for the same wires on the sheet: t1 = A[0]; t2 = A[1]; t3 = A[2];
  //   t15[7:0] = {t14, t13, t12, t11, t10, t9, t8, t7}
endmodule

module DEC4 (
  input  [3:0] A,
  output [15:0] Y
);

  wire t5, t6, t7, t8, t9, t10, t11, t12, t13, t14, t15, t16, t17, t18, t19, t20, t21, t22, t23, t24;

  not not_1 (t5, A[0]);
  not not_2 (t6, A[1]);
  not not_3 (t7, A[2]);
  not not_4 (t8, A[3]);
  and and_1 (t9, t5, t6, t7, t8);
  and and_2 (t10, A[0], t6, t7, t8);
  and and_3 (t11, t5, A[1], t7, t8);
  and and_4 (t12, A[0], A[1], t7, t8);
  and and_5 (t13, t5, t6, A[2], t8);
  and and_6 (t14, A[0], t6, A[2], t8);
  and and_7 (t15, t5, A[1], A[2], t8);
  and and_8 (t16, A[0], A[1], A[2], t8);
  and and_9 (t17, t5, t6, t7, A[3]);
  and and_10 (t18, A[0], t6, t7, A[3]);
  and and_11 (t19, t5, A[1], t7, A[3]);
  and and_12 (t20, A[0], A[1], t7, A[3]);
  and and_13 (t21, t5, t6, A[2], A[3]);
  and and_14 (t22, A[0], t6, A[2], A[3]);
  and and_15 (t23, t5, A[1], A[2], A[3]);
  and and_16 (t24, A[0], A[1], A[2], A[3]);
  assign Y = {t24, t23, t22, t21, t20, t19, t18, t17, t16, t15, t14, t13, t12, t11, t10, t9} | {t24, t23, t22, t21, t20, t19, t18, t17, t16, t15, t14, t13, t12, t11, t10, t9};  // OR_Gate or_1, 16 bits wide

  // Other names for the same wires on the sheet: t1 = A[0]; t2 = A[1]; t3 = A[2]; t4 = A[3];
  //   t25[15:0] = {t24, t23, t22, t21, t20, t19, t18, t17, t16, t15, t14, t13, t12, t11, t10, t9}
endmodule

module MUX8_8 (
  input  [7:0] D0,
  input  [7:0] D1,
  input  [7:0] D2,
  input  [7:0] D3,
  input  [7:0] D4,
  input  [7:0] D5,
  input  [7:0] D6,
  input  [7:0] D7,
  input  [2:0] S,
  output [7:0] Y
);

  wire [7:0] t1, t11, t13, t15, t17, t19, t21, t23, t25, t26;

  DEC3 dec3_1 (.A(S), .Y(t1));
  assign t11 = D0 & {8{t1[0]}};  // AND_Gate and_1, 8 bits wide
  assign t13 = D1 & {8{t1[1]}};  // AND_Gate and_2, 8 bits wide
  assign t15 = D2 & {8{t1[2]}};  // AND_Gate and_3, 8 bits wide
  assign t17 = D3 & {8{t1[3]}};  // AND_Gate and_4, 8 bits wide
  assign t19 = D4 & {8{t1[4]}};  // AND_Gate and_5, 8 bits wide
  assign t21 = D5 & {8{t1[5]}};  // AND_Gate and_6, 8 bits wide
  assign t23 = D6 & {8{t1[6]}};  // AND_Gate and_7, 8 bits wide
  assign t25 = D7 & {8{t1[7]}};  // AND_Gate and_8, 8 bits wide
  assign t26 = t11 | t13 | t15 | t17 | t19 | t21 | t23 | t25;  // OR_Gate or_1, 8 bits wide
  assign Y = t26 | t26;  // OR_Gate or_2, 8 bits wide

  // Other names for the same wires on the sheet: t2 = t1[0]; t10[7:0] = {8{t1[0]}}; t3 = t1[1]; t12[7:0] = {8{t1[1]}};
  //   t4 = t1[2]; t14[7:0] = {8{t1[2]}}; t5 = t1[3]; t16[7:0] = {8{t1[3]}}; t6 = t1[4]; t18[7:0] = {8{t1[4]}};
  //   t7 = t1[5]; t20[7:0] = {8{t1[5]}}; t8 = t1[6]; t22[7:0] = {8{t1[6]}}; t9 = t1[7]; t24[7:0] = {8{t1[7]}}
endmodule

module EQ3 (
  input  [2:0] A,
  input  [2:0] B,
  output EQ
);

  wire t5;
  wire [2:0] t1;

  assign t1 = A ^ B;  // XOR_Gate xor_1, 3 bits wide
  nor nor_1 (t5, t1[0], t1[1], t1[2]);
  or or_1 (EQ, t5, t5);

  // Other names for the same wires on the sheet: t2 = t1[0]; t3 = t1[1]; t4 = t1[2]
endmodule

module ZERO8 (
  input  [7:0] A,
  output Z
);

  wire t9;

  nor nor_1 (t9, A[0], A[1], A[2], A[3], A[4], A[5], A[6], A[7]);
  or or_1 (Z, t9, t9);

  // Other names for the same wires on the sheet: t1 = A[0]; t2 = A[1]; t3 = A[2]; t4 = A[3]; t5 = A[4]; t6 = A[5];
  //   t7 = A[6]; t8 = A[7]
endmodule

module EQ8 (
  input  [7:0] A,
  input  [7:0] B,
  output EQ
);

  wire t10;
  wire [7:0] t1;

  assign t1 = A ^ B;  // XOR_Gate xor_1, 8 bits wide
  nor nor_1 (t10, t1[0], t1[1], t1[2], t1[3], t1[4], t1[5], t1[6], t1[7]);
  or or_1 (EQ, t10, t10);

  // Other names for the same wires on the sheet: t2 = t1[0]; t3 = t1[1]; t4 = t1[2]; t5 = t1[3]; t6 = t1[4];
  //   t7 = t1[5]; t8 = t1[6]; t9 = t1[7]
endmodule

module ALU (
  input  [7:0] A,
  input  [7:0] B,
  input  [2:0] OP,
  output [7:0] R
);

  wire t10, t14, t15, t16, t17;
  wire [7:0] t1, t12, t13, t21, t22, t24, t26, t27;

  DEC3 dec3_1 (.A(OP), .Y(t1));
  or or_1 (t10, t1[1], t1[4]);
  assign t12 = B ^ {8{t10}};  // XOR_Gate xor_1, 8 bits wide
  ADD8 add8_1 (.A(A), .B(t12), .CI(t10), .S(t13), .CO(t14));
  or or_2 (t15, t1[0], t1[1]);
  not not_1 (t16, t14);
  and and_1 (t17, t1[4], t16);
  assign t21 = t13 & {8{t15}};  // AND_Gate and_2, 8 bits wide
  assign t22 = A & B;  // AND_Gate and_3, 8 bits wide
  assign t24 = t22 & {8{t1[2]}};  // AND_Gate and_4, 8 bits wide
  assign t26 = B & {8{t1[3]}};  // AND_Gate and_5, 8 bits wide
  assign t27 = t21 | t24 | t26 | {{7{1'b0}}, t17};  // OR_Gate or_3, 8 bits wide
  assign R = t27 | t27;  // OR_Gate or_4, 8 bits wide

  // Other names for the same wires on the sheet: t2 = t1[0]; t3 = t1[1]; t6 = t1[4]; t7 = t1[5]; t8 = t1[6];
  //   t9 = t1[7]; t11[7:0] = {8{t10}}; t19[0] = t17; t20[7:0] = {8{t15}}; t4 = t1[2]; t23[7:0] = {8{t1[2]}};
  //   t5 = t1[3]; t25[7:0] = {8{t1[3]}}
endmodule

module REGFILE (
  input  CLK,
  input  WE,
  input  [2:0] WA,
  input  [7:0] WD,
  input  [2:0] RA1,
  input  [2:0] RA2,
  output [7:0] RD1,
  output [7:0] RD2,
  output [7:0] R0,
  output [7:0] R1,
  output [7:0] R2,
  output [7:0] R3,
  output [7:0] R4,
  output [7:0] R5,
  output [7:0] R6,
  output [7:0] R7
);

  wire t10, t12, t14, t16, t18, t20, t22, t24, t27, t28, t31, t32;
  wire [7:0] q0, q1, q2, q3, q4, q5, q6, q7, t1, t26, t29, t30, t33;

  DEC3 dec3_1 (.A(WA), .Y(t1));
  and and_1 (t10, WE, t1[0]);
  Register #(.width(8)) register_1 (.D(WD), .en(t10), .Q(q0), .clk(CLK), .clr(1'b0));
  and and_2 (t12, WE, t1[1]);
  Register #(.width(8)) register_2 (.D(WD), .en(t12), .Q(q1), .clk(CLK), .clr(1'b0));
  and and_3 (t14, WE, t1[2]);
  Register #(.width(8)) register_3 (.D(WD), .en(t14), .Q(q2), .clk(CLK), .clr(1'b0));
  and and_4 (t16, WE, t1[3]);
  Register #(.width(8)) register_4 (.D(WD), .en(t16), .Q(q3), .clk(CLK), .clr(1'b0));
  and and_5 (t18, WE, t1[4]);
  Register #(.width(8)) register_5 (.D(WD), .en(t18), .Q(q4), .clk(CLK), .clr(1'b0));
  and and_6 (t20, WE, t1[5]);
  Register #(.width(8)) register_6 (.D(WD), .en(t20), .Q(q5), .clk(CLK), .clr(1'b0));
  and and_7 (t22, WE, t1[6]);
  Register #(.width(8)) register_7 (.D(WD), .en(t22), .Q(q6), .clk(CLK), .clr(1'b0));
  and and_8 (t24, WE, t1[7]);
  Register #(.width(8)) register_8 (.D(WD), .en(t24), .Q(q7), .clk(CLK), .clr(1'b0));
  MUX8_8 mux8_8_1 (.D0(q0), .D1(q1), .D2(q2), .D3(q3), .D4(q4), .D5(q5), .D6(q6), .D7(q7), .S(RA1), .Y(t26));
  EQ3 eq3_1 (.A(WA), .B(RA1), .EQ(t27));
  and and_9 (t28, WE, t27);
  MUX2_8 mux2_8_1 (.A(t26), .B(WD), .S(t28), .Y(t29));
  MUX8_8 mux8_8_2 (.D0(q0), .D1(q1), .D2(q2), .D3(q3), .D4(q4), .D5(q5), .D6(q6), .D7(q7), .S(RA2), .Y(t30));
  EQ3 eq3_2 (.A(WA), .B(RA2), .EQ(t31));
  and and_10 (t32, WE, t31);
  MUX2_8 mux2_8_2 (.A(t30), .B(WD), .S(t32), .Y(t33));
  assign RD1 = t29 | t29;  // OR_Gate or_1, 8 bits wide
  assign RD2 = t33 | t33;  // OR_Gate or_2, 8 bits wide
  assign R0 = q0 | q0;  // OR_Gate or_3, 8 bits wide
  assign R1 = q1 | q1;  // OR_Gate or_4, 8 bits wide
  assign R2 = q2 | q2;  // OR_Gate or_5, 8 bits wide
  assign R3 = q3 | q3;  // OR_Gate or_6, 8 bits wide
  assign R4 = q4 | q4;  // OR_Gate or_7, 8 bits wide
  assign R5 = q5 | q5;  // OR_Gate or_8, 8 bits wide
  assign R6 = q6 | q6;  // OR_Gate or_9, 8 bits wide
  assign R7 = q7 | q7;  // OR_Gate or_10, 8 bits wide

  // Other names for the same wires on the sheet: t2 = t1[0]; t3 = t1[1]; t4 = t1[2]; t5 = t1[3]; t6 = t1[4];
  //   t7 = t1[5]; t8 = t1[6]; t9 = t1[7]
endmodule

module DECODE (
  input  [15:0] INSTR,
  output [2:0] RA,
  output [2:0] RB,
  output [7:0] IMM,
  output [2:0] ALU,
  output RW,
  output MR,
  output MW,
  output UA,
  output UB,
  output BIMM,
  output KBZ,
  output KBNZ,
  output KJMP,
  output KHALT
);

  wire t22, t23, t24, t25, t26, t27, t28;
  wire [15:0] t5;

  DEC4 dec4_1 (.A(INSTR[15:12]), .Y(t5));
  or or_1 (t22, t5[0], t5[1], t5[2], t5[4], t5[6], t5[7], t5[9], t5[10], t5[11], t5[12], t5[14], t5[15]);
  or or_2 (t23, t5[1], t5[2], t5[5], t5[6], t5[7]);
  or or_3 (t24, t5[0], t5[9], t5[10], t5[11], t5[12], t5[13], t5[14], t5[15]);
  or or_4 (t25, t5[1], t5[2], t5[3], t5[4], t5[5], t5[6], t5[8], t5[13]);
  or or_5 (t26, t5[3], t5[4], t5[5], t5[7], t5[8], t5[9], t5[10], t5[13]);
  or or_6 (t27, t5[2], t5[3], t5[4], t5[5], t5[6], t5[7], t5[13]);
  or or_7 (t28, t5[1], t5[8]);
  assign RA = INSTR[11:9] | INSTR[11:9];  // OR_Gate or_8, 3 bits wide
  assign RB = INSTR[8:6] | INSTR[8:6];  // OR_Gate or_9, 3 bits wide
  assign IMM = INSTR[7:0] | INSTR[7:0];  // OR_Gate or_10, 8 bits wide
  assign ALU = {t24, t23, t22} | {t24, t23, t22};  // OR_Gate or_11, 3 bits wide
  or or_12 (RW, t25, t25);
  or or_13 (MR, t5[6], t5[6]);
  or or_14 (MW, t5[7], t5[7]);
  or or_15 (UA, t26, t26);
  or or_16 (UB, t27, t27);
  or or_17 (BIMM, t28, t28);
  or or_18 (KBZ, t5[9], t5[9]);
  or or_19 (KBNZ, t5[10], t5[10]);
  or or_20 (KJMP, t5[11], t5[11]);
  or or_21 (KHALT, t5[12], t5[12]);

  // Other names for the same wires on the sheet: t1[7:0] = INSTR[7:0]; t2[2:0] = INSTR[8:6]; t3[2:0] = INSTR[11:9];
  //   t4[3:0] = INSTR[15:12]; t6 = t5[0]; t7 = t5[1]; t8 = t5[2]; t9 = t5[3]; t10 = t5[4]; t11 = t5[5]; t12 = t5[6];
  //   t13 = t5[7]; t14 = t5[8]; t15 = t5[9]; t16 = t5[10]; t17 = t5[11]; t18 = t5[12]; t19 = t5[13]; t20 = t5[14];
  //   t21 = t5[15]; t29[2:0] = {t24, t23, t22}
endmodule

module HDU (
  input  IFID_V,
  input  [2:0] RA,
  input  [2:0] RB,
  input  UA,
  input  UB,
  input  IDEX_V,
  input  IDEX_MR,
  input  [2:0] IDEX_A,
  input  FLUSH,
  output LOADUSE,
  output STALL
);

  wire t1, t2, t3, t4, t5, t6, t7, t8;

  EQ3 eq3_1 (.A(RA), .B(IDEX_A), .EQ(t1));
  EQ3 eq3_2 (.A(RB), .B(IDEX_A), .EQ(t2));
  and and_1 (t3, UA, t1);
  and and_2 (t4, UB, t2);
  or or_1 (t5, t3, t4);
  and and_3 (t6, IFID_V, IDEX_V, IDEX_MR, t5);
  or or_2 (LOADUSE, t6, t6);
  not not_1 (t7, FLUSH);
  and and_4 (t8, t6, t7);
  or or_3 (STALL, t8, t8);
endmodule

module FWD (
  input  [2:0] SRC,
  input  USE,
  input  MEM_V,
  input  MEM_RW,
  input  MEM_MR,
  input  [2:0] MEM_RD,
  input  [7:0] MEM_RES,
  input  WB_V,
  input  WB_RW,
  input  [2:0] WB_RD,
  input  [7:0] WB_DATA,
  input  [7:0] REGV,
  output [7:0] OUT,
  output SEL_MEM,
  output SEL_WB
);

  wire t1, t2, t3, t4, t5, t6;
  wire [7:0] t7, t8;

  EQ3 eq3_1 (.A(SRC), .B(MEM_RD), .EQ(t1));
  EQ3 eq3_2 (.A(SRC), .B(WB_RD), .EQ(t2));
  not not_1 (t3, MEM_MR);
  and and_1 (t4, USE, MEM_V, MEM_RW, t3, t1);
  not not_2 (t5, t4);
  and and_2 (t6, USE, WB_V, WB_RW, t2, t5);
  MUX2_8 mux2_8_1 (.A(REGV), .B(WB_DATA), .S(t6), .Y(t7));
  MUX2_8 mux2_8_2 (.A(t7), .B(MEM_RES), .S(t4), .Y(t8));
  assign OUT = t8 | t8;  // OR_Gate or_1, 8 bits wide
  or or_2 (SEL_MEM, t4, t4);
  or or_3 (SEL_WB, t6, t6);
endmodule

module EXSTAGE (
  input  [7:0] VALA,
  input  [7:0] VALB,
  input  [7:0] IMM,
  input  [2:0] RA,
  input  [2:0] RB,
  input  UA,
  input  UB,
  input  BIMM,
  input  [2:0] ALUOP,
  input  KBZ,
  input  KBNZ,
  input  KJMP,
  input  KHALT,
  input  V,
  input  MEM_V,
  input  MEM_RW,
  input  MEM_MR,
  input  [2:0] MEM_RD,
  input  [7:0] MEM_RES,
  input  WB_V,
  input  WB_RW,
  input  [2:0] WB_RD,
  input  [7:0] WB_DATA,
  output [7:0] RES,
  output [7:0] SD,
  output TAKEN,
  output HALT_EX,
  output FLUSH,
  output [1:0] FWDA,
  output [1:0] FWDB
);

  wire t3, t4, t5, t6, t9, t10, t11, t12, t13, t14, t15, t16, t17, t18, t20, t21;
  wire [7:0] t1, t2, t7, t8;

  FWD fwd_1 (
    .SRC(RA), .USE(UA), .MEM_V(MEM_V), .MEM_RW(MEM_RW), .MEM_MR(MEM_MR), .MEM_RD(MEM_RD), .MEM_RES(MEM_RES),
    .WB_V(WB_V), .WB_RW(WB_RW), .WB_RD(WB_RD), .WB_DATA(WB_DATA), .REGV(VALA), .OUT(t1), .SEL_MEM(t3),
    .SEL_WB(t4));
  FWD fwd_2 (
    .SRC(RB), .USE(UB), .MEM_V(MEM_V), .MEM_RW(MEM_RW), .MEM_MR(MEM_MR), .MEM_RD(MEM_RD), .MEM_RES(MEM_RES),
    .WB_V(WB_V), .WB_RW(WB_RW), .WB_RD(WB_RD), .WB_DATA(WB_DATA), .REGV(VALB), .OUT(t2), .SEL_MEM(t5),
    .SEL_WB(t6));
  MUX2_8 mux2_8_1 (.A(t2), .B(IMM), .S(BIMM), .Y(t7));
  ALU alu_1 (.A(t1), .B(t7), .OP(ALUOP), .R(t8));
  ZERO8 zero8_1 (.A(t1), .Z(t9));
  and and_1 (t10, KBZ, t9);
  not not_1 (t11, t9);
  and and_2 (t12, KBNZ, t11);
  or or_1 (t13, t10, t12, KJMP);
  and and_3 (t14, V, t13);
  and and_4 (t15, V, KHALT);
  assign RES = t8 | t8;  // OR_Gate or_2, 8 bits wide
  assign SD = t1 | t1;  // OR_Gate or_3, 8 bits wide
  or or_4 (TAKEN, t14, t14);
  or or_5 (HALT_EX, t15, t15);
  or or_6 (t16, t14, t15);
  or or_7 (FLUSH, t16, t16);
  and and_5 (t17, t3, V);
  and and_6 (t18, t4, V);
  assign FWDA = {t18, t17} | {t18, t17};  // OR_Gate or_8, 2 bits wide
  and and_7 (t20, t5, V);
  and and_8 (t21, t6, V);
  assign FWDB = {t21, t20} | {t21, t20};  // OR_Gate or_9, 2 bits wide

  // Other names for the same wires on the sheet: t19[1:0] = {t18, t17}; t22[1:0] = {t21, t20}
endmodule

module SAFETY (
  input  CLK,
  input  RESET,
  input  CPU_MOTOR_EN,
  input  DOOR_CLOSED,
  input  START,
  output TRIP,
  output ACTUAL
);

  wire start_prev_q, t1, t2, t3, t4, t5, t6, t7, t8, t11, t12, trip_q;

  not not_1 (t1, CPU_MOTOR_EN);
  not not_2 (t2, start_prev_q);
  and and_1 (t3, t1, DOOR_CLOSED, START, t2);
  not not_3 (t4, DOOR_CLOSED);
  and and_2 (t5, t4, CPU_MOTOR_EN);
  or or_1 (t6, trip_q, t5);
  not not_4 (t7, t3);
  and and_3 (t8, t6, t7);
  Register #(.width(1)) register_1 (.D(t8), .en(1'b1), .Q(trip_q), .clk(CLK), .clr(RESET));
  Register #(.width(1)) register_2 (.D(START), .en(1'b1), .Q(start_prev_q), .clk(CLK), .clr(RESET));
  or or_2 (TRIP, trip_q, trip_q);
  not not_5 (t11, trip_q);
  and and_4 (t12, CPU_MOTOR_EN, DOOR_CLOSED, t11);
  or or_3 (ACTUAL, t12, t12);
endmodule

module TIMER (
  input  CLK,
  input  RESET,
  input  WE_LIM,
  input  WE_CTRL,
  input  [7:0] WDATA,
  output [7:0] CNT,
  output [7:0] LIM,
  output EN,
  output MATCH
);

  wire en_q, match_q, t2, t3, t7, t9, t10, t11, t12, t13, t14;
  wire [7:0] cnt_q, lim_q, t4, t6;

  and and_1 (t2, WE_CTRL, WDATA[1]);
  not not_1 (t3, t2);
  INC8 inc8_1 (.A(cnt_q), .S(t4));
  assign t6 = t4 & {8{t3}};  // AND_Gate and_2, 8 bits wide
  or or_1 (t7, t2, en_q);
  Register #(.width(8)) register_1 (.D(t6), .en(t7), .Q(cnt_q), .clk(CLK), .clr(RESET));
  Register #(.width(8)) register_2 (.D(WDATA), .en(WE_LIM), .Q(lim_q), .clk(CLK), .clr(RESET));
  Register #(.width(1)) register_3 (.D(WDATA[0]), .en(WE_CTRL), .Q(en_q), .clk(CLK), .clr(RESET));
  EQ8 eq8_1 (.A(t4), .B(lim_q), .EQ(t9));
  ZERO8 zero8_1 (.A(lim_q), .Z(t10));
  not not_2 (t11, t10);
  and and_3 (t12, en_q, t9, t11);
  or or_2 (t13, match_q, t12);
  and and_4 (t14, t3, t13);
  Register #(.width(1)) register_4 (.D(t14), .en(1'b1), .Q(match_q), .clk(CLK), .clr(RESET));
  assign CNT = cnt_q | cnt_q;  // OR_Gate or_3, 8 bits wide
  assign LIM = lim_q | lim_q;  // OR_Gate or_4, 8 bits wide
  or or_5 (EN, en_q, en_q);
  or or_6 (MATCH, match_q, match_q);

  // Other names for the same wires on the sheet: t5[7:0] = {8{t3}}; t8 = WDATA[0]; t1 = WDATA[1]
endmodule

module MEMSTAGE (
  input  CLK,
  input  RESET,
  input  [7:0] ADDR,
  input  [7:0] WDATA,
  input  V,
  input  MR,
  input  MW,
  input  IN_START,
  input  [1:0] IN_MODE,
  input  IN_DOOR,
  input  [7:0] IN_LEVEL,
  input  [7:0] IN_TEMP,
  input  [7:0] IN_RPM,
  output [7:0] RDATA,
  output [6:0] ACT,
  output [7:0] DISP,
  output TRIP,
  output ACTUAL,
  output [7:0] CNT,
  output [7:0] LIM,
  output EN,
  output MATCH
);

  wire t28, t29, t30, t31, t35, t36, t39, t40, t41, t42, t43, t44, t56, t59, t62, t65, t68, t71, t74, t77,
       t80, t83;
  wire [6:0] act_q;
  wire [7:0] disp_q, t33, t37, t38, t58, t61, t64, t67, t70, t73, t76, t79, t82, t85, t87, t88;
  wire [15:0] t11;

  DEC4 dec4_1 (.A(ADDR[3:0]), .Y(t11));
  and and_1 (t28, ADDR[4], ADDR[5], ADDR[6], ADDR[7]);
  not not_1 (t29, ADDR[7]);
  and and_2 (t30, V, MW);
  and and_3 (t31, t30, t29);
  RAM #(.addrWidth(7), .databus("bibus"), .dataWidth(8), .enables("line")) DRAM (
    .addr(ADDR[6:0]), .we(t31), .clk(CLK), .din(WDATA), .dout(t33));
  and and_4 (t35, t30, t28, t11[4]);
  Register #(.width(7)) register_1 (.D(WDATA[6:0]), .en(t35), .Q(act_q), .clk(CLK), .clr(RESET));
  and and_5 (t36, t30, t28, t11[5]);
  Register #(.width(8)) register_2 (.D(WDATA), .en(t36), .Q(disp_q), .clk(CLK), .clr(RESET));
  and and_6 (t41, t30, t28, t11[9]);
  and and_7 (t42, t30, t28, t11[10]);
  TIMER timer_1 (
    .CLK(CLK), .RESET(RESET), .WE_LIM(t41), .WE_CTRL(t42), .WDATA(WDATA), .CNT(t37), .LIM(t38), .EN(t39),
    .MATCH(t40));
  SAFETY safety_1 (
    .CLK(CLK), .RESET(RESET), .CPU_MOTOR_EN(act_q[2]), .DOOR_CLOSED(IN_DOOR), .START(IN_START), .TRIP(t43),
    .ACTUAL(t44));
  and and_8 (t56, t11[0], t28);
  assign t58 = {8{t56}} & {3'b000, t43, IN_DOOR, IN_MODE, IN_START};  // AND_Gate and_9, 8 bits wide
  and and_10 (t59, t11[1], t28);
  assign t61 = {8{t59}} & IN_LEVEL;  // AND_Gate and_11, 8 bits wide
  and and_12 (t62, t11[2], t28);
  assign t64 = {8{t62}} & IN_TEMP;  // AND_Gate and_13, 8 bits wide
  and and_14 (t65, t11[3], t28);
  assign t67 = {8{t65}} & IN_RPM;  // AND_Gate and_15, 8 bits wide
  and and_16 (t68, t11[4], t28);
  assign t70 = {8{t68}} & {1'b0, act_q};  // AND_Gate and_17, 8 bits wide
  and and_18 (t71, t11[5], t28);
  assign t73 = {8{t71}} & disp_q;  // AND_Gate and_19, 8 bits wide
  and and_20 (t74, t11[8], t28);
  assign t76 = {8{t74}} & t37;  // AND_Gate and_21, 8 bits wide
  and and_22 (t77, t11[9], t28);
  assign t79 = {8{t77}} & t38;  // AND_Gate and_23, 8 bits wide
  and and_24 (t80, t11[10], t28);
  assign t82 = {8{t80}} & {{7{1'b0}}, t39};  // AND_Gate and_25, 8 bits wide
  and and_26 (t83, t11[11], t28);
  assign t85 = {8{t83}} & {{7{1'b0}}, t40};  // AND_Gate and_27, 8 bits wide
  assign t87 = t33 & {8{t29}};  // AND_Gate and_28, 8 bits wide
  assign t88 = t87 | t58 | t61 | t64 | t67 | t70 | t73 | t76 | t79 | t82 | t85;  // OR_Gate or_1, 8 bits wide
  assign RDATA = t88 | t88;  // OR_Gate or_2, 8 bits wide
  assign ACT = act_q | act_q;  // OR_Gate or_3, 7 bits wide
  assign DISP = disp_q | disp_q;  // OR_Gate or_4, 8 bits wide
  or or_5 (TRIP, t43, t43);
  or or_6 (ACTUAL, t44, t44);
  assign CNT = t37 | t37;  // OR_Gate or_7, 8 bits wide
  assign LIM = t38 | t38;  // OR_Gate or_8, 8 bits wide
  or or_9 (EN, t39, t39);
  or or_10 (MATCH, t40, t40);

  // Other names for the same wires on the sheet: t1 = ADDR[0]; t10[3:0] = ADDR[3:0]; t32[6:0] = ADDR[6:0];
  //   t2 = ADDR[1]; t3 = ADDR[2]; t4 = ADDR[3]; t5 = ADDR[4]; t9[3:0] = ADDR[7:4]; t6 = ADDR[5]; t7 = ADDR[6];
  //   t8 = ADDR[7]; t12 = t11[0]; t13 = t11[1]; t14 = t11[2]; t15 = t11[3]; t16 = t11[4]; t17 = t11[5]; t18 = t11[6];
  //   t19 = t11[7]; t20 = t11[8]; t21 = t11[9]; t22 = t11[10]; t23 = t11[11]; t24 = t11[12]; t25 = t11[13];
  //   t26 = t11[14]; t27 = t11[15]; t50[4:0] = {t43, IN_DOOR, IN_MODE, IN_START}; t51[6:0] = act_q; t45 = act_q[2];
  //   t53[0] = t39; t55[0] = t40; t57[7:0] = {8{t56}}; t60[7:0] = {8{t59}}; t63[7:0] = {8{t62}}; t66[7:0] = {8{t65}};
  //   t69[7:0] = {8{t68}}; t72[7:0] = {8{t71}}; t75[7:0] = {8{t74}}; t78[7:0] = {8{t77}}; t81[7:0] = {8{t80}};
  //   t84[7:0] = {8{t83}}; t86[7:0] = {8{t29}}; t34[6:0] = WDATA[6:0]
endmodule

module main (
  input  RESET,
  input  START,
  input  [1:0] MODE,
  input  DOOR_CLOSED,
  input  [7:0] WATER_LEVEL,
  input  [7:0] TEMP,
  input  [7:0] DRUM_RPM,
  output VALVE_IN,
  output HEATER,
  output MOTOR_EN_CMD,
  output MOTOR_EN_ACTUAL,
  output MOTOR_DIR,
  output PUMP_OUT,
  output DOOR_LOCK,
  output BUZZER,
  output [7:0] DISPLAY,
  output TRIP,
  output HALTED,
  output [7:0] PC,
  output [7:0] R0_,
  output [7:0] R1_,
  output [7:0] R2_,
  output [7:0] R3_,
  output [7:0] R4_,
  output [7:0] R5_,
  output [7:0] R6_,
  output [7:0] R7_,
  output [7:0] COUNT,
  output [7:0] LIMIT,
  output TIMER_EN,
  output MATCH,
  output [7:0] ACT,
  output V_IFID,
  output V_IDEX,
  output V_EXMEM,
  output V_MEMWB,
  output STALL_,
  output FLUSH_,
  output [1:0] FWD_A,
  output [1:0] FWD_B
);

  wire CLK, exmem_mr, exmem_mw, exmem_rw, exmem_v, FLUSH, halt_ex, halted_t, idex_bimm, idex_kbnz, idex_kbz,
       idex_khalt, idex_kjmp, idex_mr, idex_mw, idex_rw, idex_ua, idex_ub, idex_v, ifid_v, memwb_rw, memwb_v,
       STALL, t5, t6, t7, t8, t9, t10, t13, t14, t15, t20, t21, t22, t23, t24, t25, t26, t27, t28, t29, t30,
       t33, t34, t35, t65, t66, t69, t70, taken;
  wire [1:0] t53, t54;
  wire [2:0] exmem_rd, idex_a, idex_alu, idex_b, memwb_rd, t16, t17, t19;
  wire [6:0] t63;
  wire [7:0] exmem_res, exmem_sd, idex_imm, idex_vala, idex_valb, memwb_data, R0, R1, R2, R3, R4, R5, R6, R7,
       t1, t2, t3, t4, t18, t31, t32, t62, t64, t67, t68, t71;
  wire [15:0] ifid_instr, t12;

  Clock u_CLK (.out(CLK));
  INC8 inc8_1 (.A(PC), .S(t1));
  MUX2_8 mux2_8_1 (.A(t1), .B(idex_imm), .S(taken), .Y(t4));
  not not_1 (t5, STALL);
  not not_2 (t6, halted_t);
  not not_3 (t7, halt_ex);
  and and_1 (t8, t6, t7, t5);
  or or_1 (t9, taken, t8);
  Register #(.width(8)) register_1 (.D(t4), .en(t9), .Q(PC), .clk(CLK), .clr(RESET));
  or or_2 (t10, halted_t, halt_ex);
  Register #(.width(1)) register_2 (.D(t10), .en(1'b1), .Q(halted_t), .clk(CLK), .clr(RESET));
  ROM #(.addrWidth(8), .dataWidth(16)) IROM (.addr(PC), .data(t12));
  Register #(.width(16)) register_3 (.D(t12), .en(t5), .Q(ifid_instr), .clk(CLK), .clr(RESET));
  not not_4 (t13, FLUSH);
  not not_5 (t14, halted_t);
  and and_2 (t15, t13, t14);
  Register #(.width(1)) register_4 (.D(t15), .en(t5), .Q(ifid_v), .clk(CLK), .clr(RESET));
  DECODE decode_1 (
    .INSTR(ifid_instr), .RA(t16), .RB(t17), .IMM(t18), .ALU(t19), .RW(t20), .MR(t21), .MW(t22), .UA(t23),
    .UB(t24), .BIMM(t25), .KBZ(t26), .KBNZ(t27), .KJMP(t28), .KHALT(t29));
  HDU hdu_1 (
    .IFID_V(ifid_v), .RA(t16), .RB(t17), .UA(t23), .UB(t24), .IDEX_V(idex_v), .IDEX_MR(idex_mr),
    .IDEX_A(idex_a), .FLUSH(FLUSH), .LOADUSE(t30), .STALL(STALL));
  and and_3 (t33, memwb_v, memwb_rw);
  REGFILE regfile_1 (
    .CLK(CLK), .WE(t33), .WA(memwb_rd), .WD(memwb_data), .RA1(t16), .RA2(t17), .RD1(t31), .RD2(t32), .R0(R0),
    .R1(R1), .R2(R2), .R3(R3), .R4(R4), .R5(R5), .R6(R6), .R7(R7));
  not not_6 (t34, FLUSH);
  and and_4 (t35, ifid_v, t5, t34);
  Register #(.width(1)) register_5 (.D(t35), .en(1'b1), .Q(idex_v), .clk(CLK), .clr(RESET));
  Register #(.width(3)) register_6 (.D(t16), .en(1'b1), .Q(idex_a), .clk(CLK), .clr(RESET));
  Register #(.width(3)) register_7 (.D(t17), .en(1'b1), .Q(idex_b), .clk(CLK), .clr(RESET));
  Register #(.width(8)) register_8 (.D(t18), .en(1'b1), .Q(idex_imm), .clk(CLK), .clr(RESET));
  Register #(.width(3)) register_9 (.D(t19), .en(1'b1), .Q(idex_alu), .clk(CLK), .clr(RESET));
  Register #(.width(1)) register_10 (.D(t20), .en(1'b1), .Q(idex_rw), .clk(CLK), .clr(RESET));
  Register #(.width(1)) register_11 (.D(t21), .en(1'b1), .Q(idex_mr), .clk(CLK), .clr(RESET));
  Register #(.width(1)) register_12 (.D(t22), .en(1'b1), .Q(idex_mw), .clk(CLK), .clr(RESET));
  Register #(.width(1)) register_13 (.D(t23), .en(1'b1), .Q(idex_ua), .clk(CLK), .clr(RESET));
  Register #(.width(1)) register_14 (.D(t24), .en(1'b1), .Q(idex_ub), .clk(CLK), .clr(RESET));
  Register #(.width(1)) register_15 (.D(t25), .en(1'b1), .Q(idex_bimm), .clk(CLK), .clr(RESET));
  Register #(.width(1)) register_16 (.D(t26), .en(1'b1), .Q(idex_kbz), .clk(CLK), .clr(RESET));
  Register #(.width(1)) register_17 (.D(t27), .en(1'b1), .Q(idex_kbnz), .clk(CLK), .clr(RESET));
  Register #(.width(1)) register_18 (.D(t28), .en(1'b1), .Q(idex_kjmp), .clk(CLK), .clr(RESET));
  Register #(.width(1)) register_19 (.D(t29), .en(1'b1), .Q(idex_khalt), .clk(CLK), .clr(RESET));
  Register #(.width(8)) register_20 (.D(t31), .en(1'b1), .Q(idex_vala), .clk(CLK), .clr(RESET));
  Register #(.width(8)) register_21 (.D(t32), .en(1'b1), .Q(idex_valb), .clk(CLK), .clr(RESET));
  EXSTAGE exstage_1 (
    .VALA(idex_vala), .VALB(idex_valb), .IMM(idex_imm), .RA(idex_a), .RB(idex_b), .UA(idex_ua), .UB(idex_ub),
    .BIMM(idex_bimm), .ALUOP(idex_alu), .KBZ(idex_kbz), .KBNZ(idex_kbnz), .KJMP(idex_kjmp),
    .KHALT(idex_khalt), .V(idex_v), .MEM_V(exmem_v), .MEM_RW(exmem_rw), .MEM_MR(exmem_mr), .MEM_RD(exmem_rd),
    .MEM_RES(exmem_res), .WB_V(memwb_v), .WB_RW(memwb_rw), .WB_RD(memwb_rd), .WB_DATA(memwb_data), .RES(t2),
    .SD(t3), .TAKEN(taken), .HALT_EX(halt_ex), .FLUSH(FLUSH), .FWDA(t53), .FWDB(t54));
  Register #(.width(1)) register_22 (.D(idex_v), .en(1'b1), .Q(exmem_v), .clk(CLK), .clr(RESET));
  Register #(.width(1)) register_23 (.D(idex_rw), .en(1'b1), .Q(exmem_rw), .clk(CLK), .clr(RESET));
  Register #(.width(1)) register_24 (.D(idex_mr), .en(1'b1), .Q(exmem_mr), .clk(CLK), .clr(RESET));
  Register #(.width(1)) register_25 (.D(idex_mw), .en(1'b1), .Q(exmem_mw), .clk(CLK), .clr(RESET));
  Register #(.width(3)) register_26 (.D(idex_a), .en(1'b1), .Q(exmem_rd), .clk(CLK), .clr(RESET));
  Register #(.width(8)) register_27 (.D(t2), .en(1'b1), .Q(exmem_res), .clk(CLK), .clr(RESET));
  Register #(.width(8)) register_28 (.D(t3), .en(1'b1), .Q(exmem_sd), .clk(CLK), .clr(RESET));
  MEMSTAGE memstage_1 (
    .CLK(CLK), .RESET(RESET), .ADDR(exmem_res), .WDATA(exmem_sd), .V(exmem_v), .MR(exmem_mr), .MW(exmem_mw),
    .IN_START(START), .IN_MODE(MODE), .IN_DOOR(DOOR_CLOSED), .IN_LEVEL(WATER_LEVEL), .IN_TEMP(TEMP),
    .IN_RPM(DRUM_RPM), .RDATA(t62), .ACT(t63), .DISP(t64), .TRIP(t65), .ACTUAL(t66), .CNT(t67), .LIM(t68),
    .EN(t69), .MATCH(t70));
  MUX2_8 mux2_8_2 (.A(exmem_res), .B(t62), .S(exmem_mr), .Y(t71));
  Register #(.width(1)) register_29 (.D(exmem_v), .en(1'b1), .Q(memwb_v), .clk(CLK), .clr(RESET));
  Register #(.width(1)) register_30 (.D(exmem_rw), .en(1'b1), .Q(memwb_rw), .clk(CLK), .clr(RESET));
  Register #(.width(3)) register_31 (.D(exmem_rd), .en(1'b1), .Q(memwb_rd), .clk(CLK), .clr(RESET));
  Register #(.width(8)) register_32 (.D(t71), .en(1'b1), .Q(memwb_data), .clk(CLK), .clr(RESET));
  or or_3 (VALVE_IN, t63[0], t63[0]);
  or or_4 (HEATER, t63[1], t63[1]);
  or or_5 (MOTOR_EN_CMD, t63[2], t63[2]);
  or or_6 (MOTOR_EN_ACTUAL, t66, t66);
  or or_7 (MOTOR_DIR, t63[3], t63[3]);
  or or_8 (PUMP_OUT, t63[4], t63[4]);
  or or_9 (DOOR_LOCK, t63[5], t63[5]);
  or or_10 (BUZZER, t63[6], t63[6]);
  assign DISPLAY = t64 | t64;  // OR_Gate or_11, 8 bits wide
  or or_12 (TRIP, t65, t65);
  or or_13 (HALTED, halted_t, halted_t);
  assign R0_ = R0 | R0;  // OR_Gate or_14, 8 bits wide
  assign R1_ = R1 | R1;  // OR_Gate or_15, 8 bits wide
  assign R2_ = R2 | R2;  // OR_Gate or_16, 8 bits wide
  assign R3_ = R3 | R3;  // OR_Gate or_17, 8 bits wide
  assign R4_ = R4 | R4;  // OR_Gate or_18, 8 bits wide
  assign R5_ = R5 | R5;  // OR_Gate or_19, 8 bits wide
  assign R6_ = R6 | R6;  // OR_Gate or_20, 8 bits wide
  assign R7_ = R7 | R7;  // OR_Gate or_21, 8 bits wide
  assign COUNT = t67 | t67;  // OR_Gate or_22, 8 bits wide
  assign LIMIT = t68 | t68;  // OR_Gate or_23, 8 bits wide
  or or_24 (TIMER_EN, t69, t69);
  or or_25 (MATCH, t70, t70);
  assign ACT = {1'b0, t63} | {1'b0, t63};  // OR_Gate or_26, 8 bits wide
  or or_27 (V_IFID, ifid_v, ifid_v);
  or or_28 (V_IDEX, idex_v, idex_v);
  or or_29 (V_EXMEM, exmem_v, exmem_v);
  or or_30 (V_MEMWB, memwb_v, memwb_v);
  or or_31 (STALL_, STALL, STALL);
  or or_32 (FLUSH_, FLUSH, FLUSH);
  assign FWD_A = t53 | t53;  // OR_Gate or_33, 2 bits wide
  assign FWD_B = t54 | t54;  // OR_Gate or_34, 2 bits wide

  // Other names for the same wires on the sheet: t76 = t63[0]; t84[6:0] = t63; t77 = t63[1]; t78 = t63[2];
  //   t79 = t63[3]; t80 = t63[4]; t81 = t63[5]; t82 = t63[6]

  // Notes on the sheet:
  //   ELL782 A2 - 5-stage pipelined washing-machine microcontroller (gate-level)
  //   contents of IROM (hex, n*v repeats v):
  //   1ef4 1c00 7dc0 1efa 7dc0 1ef5 7dc0 1ef0 65c0 2080 1209 5040 4040 900f b007 1202 5440 9416 1696 1802
  //   1a0f b019 1664 1801 1a0a 1ef4 1c20 7dc0 1ef0 61c0 1208 5040 901d 1ef5 1010 3080 71c0 1ef4 1c21 7dc0
  //   1ef1 63c0 d2c0 922d b029 1ef4 1c20 7dc0 1ef5 1020 3080 71c0 1ef9 100a 71c0 1efa 1003 71c0 1ef4 1c24
  //   7dc0 1efb 61c0 903e 1efa 1003 71c0 1ef4 1c2c 7dc0 1efb 61c0 9047 88ff a837 1ef4 1c20 7dc0 1ef5 1030
  //   3080 71c0 1ef4 1c30 7dc0 1ef1 63c0 1005 d040 905b b056 1ef5 1040 3080 71c0 1ef9 7bc0 1efa 1003 71c0
  //   1ef4 1c34 7dc0 1efb 61c0 9068 1ef4 1c20 7dc0 1ef0 61c0 1210 5040 a07c 1ef4 1c40 7dc0 1efa 1000 71c0
  //   1ef5 10ff 71c0 c000 1ef4 1c00 7dc0 1ef5 10ee 71c0 c000 0 0 0 0 0 0 0 0 0 0 0 0 0 0 0 0 0 0 0 0 0 0 0
  //   0 0 0 0 0 0 0 0 0 0 0 0 0 0 0 0 0 0 0 0 0 0 0 0 0 0 0 0 0 0 0 0 0 0 0 0 0 0 0 0 0 0 0 0 0 0 0 0 0 0
  //   0 0 0 0 0 0 0 0 0 0 0 0 0 0 0 0 0 0 0 0 0 0 0 0 0 0 0 0 0 0 0 0 0 0 0 0 0 0 0 0 0 0 0 0 0 0 0 0 0 0
  //   0 0
endmodule
